# Fritzing sketch GoodLight_BadUSB_schematic (saved by Fritzing 0.9.3b)
breadboards: 1

parts:
  Part1 = Arduino Uno (Rev3)
  R1 = Resistor [tolerance=±5% resistance=220 package=THT]
  R2 = Photocell (LDR) [package=THT]
  R3 = Resistor [tolerance=±5% resistance=220 package=THT]
  LED1 = LED - 5mm [color="Yellow (592nm)" package="5 mm [THT]"]
  SG1 = Buzzer 12mm [package=buzzer-12mm-ns]
  R4 = Resistor [tolerance=±5% resistance=220 package=THT]
  LCD1 = LCD screen
  R5 = Resistor [tolerance=±5% resistance=220 package=THT]
  R6 = Trimmer Potentiometer [maximum_resistance=10kΩ package=THT]

nets (from the schematic view):
  N1: Part1.D8, SG1.2
  N2: Part1.D9_PWM, R3.Pin_0
  N3: Part1.D11_PWM/MOSI, LCD1.E
  N4: Part1.D12/MISO, LCD1.RS
  N5: Part1.D2, LCD1.DB7
  N6: Part1.D3_PWM, LCD1.DB6
  N7: Part1.D4, LCD1.DB5
  N8: Part1.D5_PWM, LCD1.DB4
  N9: Part1.5V, R2.pin_0, R5.Pin_1, R6.leg1
  GND: Part1.GND, R1.Pin_1, R4.Pin_1, LCD1.VSS, LCD1.R/W
  N10: R1.Pin_0, R2.pin_1
  N11: R3.Pin_1, LED1.anode, LCD1.LED-, R6.leg2
  N12: SG1.1, R4.Pin_0
  N13: LCD1.V0, R6.wiper
  N14: LCD1.LED+, R5.Pin_0
